// Logisim project Rom.circ as structural Verilog: 1 circuit, main circuit main
module main (
  input  in_1,
  input  in_2,
  input  in_3,
  input  in_4,
  input  in_5,
  input  in_6,
  input  in_7,
  input  in_8,
  input  in_9,
  input  in_10,
  input  in_11,
  input  in_12,
  input  in_13,
  input  in_14,
  input  in_15,
  input  in_16,
  input  in_17,
  input  in_18,
  input  in_19,
  input  in_20,
  input  in_21,
  input  in_22,
  input  in_23,
  input  in_24,
  input  in_25,
  input  in_26,
  input  in_27,
  input  in_28,
  input  in_29,
  input  in_30,
  input  in_31,
  input  in_32,
  input  in_33,
  input  in_34,
  input  in_35,
  input  in_36,
  input  in_37,
  input  in_38,
  input  in_39,
  input  in_40,
  input  in_41,
  input  in_42,
  input  in_43,
  input  in_44,
  input  in_45,
  input  in_46,
  input  in_47,
  input  in_48,
  input  in_49,
  input  in_50,
  input  in_51,
  input  in_52,
  input  in_53,
  input  in_54,
  input  in_55,
  input  in_56,
  input  in_57,
  input  in_58,
  input  in_59,
  input  in_60,
  input  in_61,
  input  in_62,
  input  in_63,
  input  in_64
);

  wire controlled_buffer_1_out, controlled_buffer_5_out, controlled_buffer_6_out, controlled_buffer_7_out,
       undriven, undriven_2, undriven_3, undriven_4, undriven_5, undriven_6, undriven_7, undriven_8,
       undriven_9, undriven_10, undriven_11, undriven_12, undriven_13, undriven_14, undriven_15, undriven_16;

  assign controlled_buffer_1_out = undriven ? in_1 : 1'bz;  // Controlled_Buffer controlled_buffer_1
  assign controlled_buffer_1_out = undriven_2 ? in_17 : 1'bz;  // Controlled_Buffer controlled_buffer_2
  assign controlled_buffer_1_out = undriven_3 ? in_33 : 1'bz;  // Controlled_Buffer controlled_buffer_3
  assign controlled_buffer_1_out = undriven_4 ? in_49 : 1'bz;  // Controlled_Buffer controlled_buffer_4
  assign controlled_buffer_5_out = undriven ? in_2 : 1'bz;  // Controlled_Buffer controlled_buffer_5
  assign controlled_buffer_6_out = undriven ? in_4 : 1'bz;  // Controlled_Buffer controlled_buffer_6
  assign controlled_buffer_7_out = undriven ? in_3 : 1'bz;  // Controlled_Buffer controlled_buffer_7
  assign controlled_buffer_5_out = undriven_2 ? in_18 : 1'bz;  // Controlled_Buffer controlled_buffer_8
  assign controlled_buffer_7_out = undriven_2 ? in_19 : 1'bz;  // Controlled_Buffer controlled_buffer_9
  assign controlled_buffer_6_out = undriven_2 ? in_20 : 1'bz;  // Controlled_Buffer controlled_buffer_10
  assign controlled_buffer_6_out = undriven_3 ? in_36 : 1'bz;  // Controlled_Buffer controlled_buffer_11
  assign controlled_buffer_7_out = undriven_3 ? in_35 : 1'bz;  // Controlled_Buffer controlled_buffer_12
  assign controlled_buffer_5_out = undriven_3 ? in_34 : 1'bz;  // Controlled_Buffer controlled_buffer_13
  assign controlled_buffer_7_out = undriven_4 ? in_51 : 1'bz;  // Controlled_Buffer controlled_buffer_14
  assign controlled_buffer_5_out = undriven_4 ? in_50 : 1'bz;  // Controlled_Buffer controlled_buffer_15
  assign controlled_buffer_6_out = undriven_4 ? in_52 : 1'bz;  // Controlled_Buffer controlled_buffer_16
  assign controlled_buffer_5_out = undriven_5 ? in_6 : 1'bz;  // Controlled_Buffer controlled_buffer_17
  assign controlled_buffer_1_out = undriven_5 ? in_5 : 1'bz;  // Controlled_Buffer controlled_buffer_18
  assign controlled_buffer_5_out = undriven_6 ? in_22 : 1'bz;  // Controlled_Buffer controlled_buffer_19
  assign controlled_buffer_1_out = undriven_6 ? in_21 : 1'bz;  // Controlled_Buffer controlled_buffer_20
  assign controlled_buffer_1_out = undriven_7 ? in_37 : 1'bz;  // Controlled_Buffer controlled_buffer_21
  assign controlled_buffer_5_out = undriven_7 ? in_38 : 1'bz;  // Controlled_Buffer controlled_buffer_22
  assign controlled_buffer_5_out = undriven_8 ? in_54 : 1'bz;  // Controlled_Buffer controlled_buffer_23
  assign controlled_buffer_1_out = undriven_8 ? in_53 : 1'bz;  // Controlled_Buffer controlled_buffer_24
  assign controlled_buffer_6_out = undriven_5 ? in_8 : 1'bz;  // Controlled_Buffer controlled_buffer_25
  assign controlled_buffer_7_out = undriven_5 ? in_7 : 1'bz;  // Controlled_Buffer controlled_buffer_26
  assign controlled_buffer_7_out = undriven_6 ? in_23 : 1'bz;  // Controlled_Buffer controlled_buffer_27
  assign controlled_buffer_6_out = undriven_6 ? in_24 : 1'bz;  // Controlled_Buffer controlled_buffer_28
  assign controlled_buffer_7_out = undriven_7 ? in_39 : 1'bz;  // Controlled_Buffer controlled_buffer_29
  assign controlled_buffer_6_out = undriven_7 ? in_40 : 1'bz;  // Controlled_Buffer controlled_buffer_30
  assign controlled_buffer_6_out = undriven_8 ? in_56 : 1'bz;  // Controlled_Buffer controlled_buffer_31
  assign controlled_buffer_7_out = undriven_8 ? in_55 : 1'bz;  // Controlled_Buffer controlled_buffer_32
  assign controlled_buffer_1_out = undriven_9 ? in_9 : 1'bz;  // Controlled_Buffer controlled_buffer_33
  assign controlled_buffer_5_out = undriven_9 ? in_10 : 1'bz;  // Controlled_Buffer controlled_buffer_34
  assign controlled_buffer_7_out = undriven_9 ? in_11 : 1'bz;  // Controlled_Buffer controlled_buffer_35
  assign controlled_buffer_7_out = undriven_10 ? in_27 : 1'bz;  // Controlled_Buffer controlled_buffer_36
  assign controlled_buffer_1_out = undriven_10 ? in_25 : 1'bz;  // Controlled_Buffer controlled_buffer_37
  assign controlled_buffer_5_out = undriven_10 ? in_26 : 1'bz;  // Controlled_Buffer controlled_buffer_38
  assign controlled_buffer_5_out = undriven_11 ? in_42 : 1'bz;  // Controlled_Buffer controlled_buffer_39
  assign controlled_buffer_1_out = undriven_11 ? in_41 : 1'bz;  // Controlled_Buffer controlled_buffer_40
  assign controlled_buffer_7_out = undriven_11 ? in_43 : 1'bz;  // Controlled_Buffer controlled_buffer_41
  assign controlled_buffer_7_out = undriven_12 ? in_59 : 1'bz;  // Controlled_Buffer controlled_buffer_42
  assign controlled_buffer_1_out = undriven_12 ? in_57 : 1'bz;  // Controlled_Buffer controlled_buffer_43
  assign controlled_buffer_5_out = undriven_12 ? in_58 : 1'bz;  // Controlled_Buffer controlled_buffer_44
  assign controlled_buffer_6_out = undriven_9 ? in_12 : 1'bz;  // Controlled_Buffer controlled_buffer_45
  assign controlled_buffer_1_out = undriven_13 ? in_13 : 1'bz;  // Controlled_Buffer controlled_buffer_46
  assign controlled_buffer_1_out = undriven_14 ? in_29 : 1'bz;  // Controlled_Buffer controlled_buffer_47
  assign controlled_buffer_6_out = undriven_10 ? in_28 : 1'bz;  // Controlled_Buffer controlled_buffer_48
  assign controlled_buffer_6_out = undriven_11 ? in_44 : 1'bz;  // Controlled_Buffer controlled_buffer_49
  assign controlled_buffer_1_out = undriven_15 ? in_45 : 1'bz;  // Controlled_Buffer controlled_buffer_50
  assign controlled_buffer_1_out = undriven_16 ? in_61 : 1'bz;  // Controlled_Buffer controlled_buffer_51
  assign controlled_buffer_6_out = undriven_12 ? in_60 : 1'bz;  // Controlled_Buffer controlled_buffer_52
  assign controlled_buffer_7_out = undriven_13 ? in_15 : 1'bz;  // Controlled_Buffer controlled_buffer_53
  assign controlled_buffer_5_out = undriven_13 ? in_14 : 1'bz;  // Controlled_Buffer controlled_buffer_54
  assign controlled_buffer_5_out = undriven_14 ? in_30 : 1'bz;  // Controlled_Buffer controlled_buffer_55
  assign controlled_buffer_7_out = undriven_14 ? in_31 : 1'bz;  // Controlled_Buffer controlled_buffer_56
  assign controlled_buffer_7_out = undriven_15 ? in_47 : 1'bz;  // Controlled_Buffer controlled_buffer_57
  assign controlled_buffer_5_out = undriven_15 ? in_46 : 1'bz;  // Controlled_Buffer controlled_buffer_58
  assign controlled_buffer_5_out = undriven_16 ? in_62 : 1'bz;  // Controlled_Buffer controlled_buffer_59
  assign controlled_buffer_7_out = undriven_16 ? in_63 : 1'bz;  // Controlled_Buffer controlled_buffer_60
  assign controlled_buffer_6_out = undriven_13 ? in_16 : 1'bz;  // Controlled_Buffer controlled_buffer_61
  assign controlled_buffer_6_out = undriven_14 ? in_32 : 1'bz;  // Controlled_Buffer controlled_buffer_62
  assign controlled_buffer_6_out = undriven_15 ? in_48 : 1'bz;  // Controlled_Buffer controlled_buffer_63
  assign controlled_buffer_6_out = undriven_16 ? in_64 : 1'bz;  // Controlled_Buffer controlled_buffer_64
endmodule
